# Fritzing sketch LM317-Basic (saved by Fritzing 0.8.5b)
circuit board: 8.46667cm x 5.64444cm
breadboards: 1

parts:
  R1 = Resistor [tolerance=±5% resistance=240 package=THT]
  C2 = Tantalum Capacitor [capacitance=1µF package="100 mil [THT, tantalum]"]
  U2 = Voltage Regulator - Variable [package="TO220 [THT]"]
  C1 = Tantalum Capacitor [capacitance=1µF package="100 mil [THT, tantalum]"]
  R3 = Trimmer Potentiometer [maximum_resistance=10kΩ package=THT]

nets (from the schematic view):
  N1: R1.Pin_0, U2.OUT
  N2: R1.Pin_1, C1.+
  GND: C2.-, C1.-, R3.wiper
  5V: C2.+, U2.IN
  N3: U2.ADJ, R3.leg2
